# Fritzing sketch arduino-ohm-law (saved by Fritzing 0.9.3b)
breadboards: 1

parts:
  Componente1 = Arduino Uno (Rev3)
  R1 = Resistor [tolerance=±5% resistance=220 package=THT]
  R2 = Trimmer Potentiometer [maximum_resistance=10kΩ package=THT]
  MAX471_Current_and_Voltage_Sensor1 = MAX471 Current and Voltage Sensor Module
  VCC1 = Battery block 9V  # not connected

nets:
  N1: Componente1.A0, MAX471_Current_and_Voltage_Sensor1.AT
  N2: Componente1.A1, R1.Pin_0, R2.leg2
  N3: Componente1.GND, MAX471_Current_and_Voltage_Sensor1.GND#13
  N4: R1.Pin_1, MAX471_Current_and_Voltage_Sensor1.GND#10
  N5: R2.leg1, MAX471_Current_and_Voltage_Sensor1.VOUT

custom parts:
  MAX471 Current and Voltage Sensor Module: The MAX471 current and voltage sensor module is a bidirectional, highside current-sense amplifier. The current measurement maximum is 3 amps and the voltage measurement range is 3 to 25 volts. The operating voltage range is 3 to 36 volts.
